# Fritzing sketch truck (saved by Fritzing 0.8.3b)
breadboards: 1

parts:
  Part1 = Arduino Uno (Rev3)
  Q1 = NPN-Transistor [package="TO92 [THT]"]
  Q2 = NPN-Transistor [package="TO92 [THT]"]
  Q3 = NPN-Transistor [package="TO92 [THT]"]
  R2 = Resistor [tolerance=±5% resistance=100k package=THT]
  R3 = Resistor [tolerance=±5% resistance=100k package=THT]
  R4 = Resistor [tolerance=±5% resistance=100k package=THT]
  LED1 = LED - 5mm [color="Red (633nm)" package="5 mm [THT]"]
  LED2 = LED - 5mm [color="Red (633nm)" package="5 mm [THT]"]
  LED3 = LED - 5mm [color="Red (633nm)" package="5 mm [THT]"]
  VCC1 = 4 x AAA Battery Mount

nets:
  N1: Part1.ICSP_MISO, Part1.D12/MISO, Q2.B, R3.Pin_0
  N2: Part1.ICSP_SCK, Part1.D13/SCK, Q3.B, R2.Pin_0
  N3: Part1.ICSP_MOSI, Part1.D11_PWM/MOSI, Q1.B, R4.Pin_0
  N4: Part1.GND, R2.Pin_1, R3.Pin_1, R4.Pin_1
  N5: Q1.E, LED3.anode
  N6: Q1.C, Q2.C, Q3.C, VCC1.+
  N7: Q2.E, LED1.anode
  N8: Q3.E, LED2.anode
  N9: LED1.cathode, LED2.cathode, LED3.cathode, VCC1.-
